# Fritzing sketch testcodeafterday1ofcode (saved by Fritzing 0.8.7b)
breadboards: 1

parts:
  Part1 = SRF05 Ultrasonic Rangefinder
  Part2 = Arduino Nano (Rev3.0)
  LED1 = LED - 5mm [color="Red (633nm)" package="5 mm [THT]"]
  GREen_led = LED - 5mm [color="Green (560nm)" package="5 mm [THT]"]
  R1 = Resistor [tolerance=±5% resistance=220 package=THT]
  R2 = Resistor [tolerance=±5% resistance=220 package=THT]
  J1 = Basic Servo

nets:
  VCC: Part1.VCC, Part2.5V, J1.vcc
  N1: Part1.Trig, Part2.D11/MOSI
  N2: Part1.Echo, Part2.D12/MISO
  GND: Part1.GND, Part2.GND, LED1.cathode, GREen_led.cathode, J1.gnd
  N3: Part2.D5, J1.pulse
  N4: LED1.anode, R2.Pin_0
  N5: GREen_led.anode, R1.Pin_0
